# Fritzing sketch Breadboard Sketch (saved by Fritzing 0.9.3b)
breadboards: 2

parts:
  Part1 = Arduino Uno (Rev3)
  U1 = 74HC595 [package="DIP16 [THT]"]
  U2 = 74HC595 [package="DIP16 [THT]"]
  Disp1 = LBT2088AH [part_number=LBT2088AH]
  S1 = Pushbutton [package="[THT]"]
  R1 = Resistor [tolerance=±5% resistance=220 package=THT]
  S2 = Pushbutton [package="[THT]"]
  R2 = Resistor [tolerance=±5% resistance=220 package=THT]

nets:
  N1: Part1.D8, U1.ST_CP
  N2: Part1.D10_PWM/SS, U1.SH_CP
  N3: Part1.D11_PWM/MOSI, U1.DS
  N4: Part1.D4, R1.Pin_1
  N5: Part1.D5_PWM, R2.Pin_1
  VCC: Part1.5V, U1.MR, U1.VCC, U2.MR, U2.VCC, S1.Pin_3, S1.Pin_4, S2.Pin_3, S2.Pin_4
  GND: Part1.GND, U1.GND, U1.OE, U2.GND, U2.OE, S1.Pin_1, S1.Pin_2, R1.Pin_0, S2.Pin_1, S2.Pin_2, R2.Pin_0
  N6: U1.Q1, Disp1.pin2
  N7: U1.Q2, Disp1.pin_3
  N8: U1.Q3, Disp1.pin_4
  N9: U1.Q4, Disp1.pin_16
  N10: U1.Q5, Disp1.pin_15
  N11: U1.Q6, Disp1.pin_14
  N12: U1.Q7, Disp1.pin_13
  N13: U1.Q7', U2.DS
  N14: U1.Q0, Disp1.pin1
  N15: U2.Q1, Disp1.pin_7
  N16: U2.Q2, Disp1.pin_6
  N17: U2.Q3, Disp1.pin_5
  N18: U2.Q4, Disp1.pin_9
  N19: U2.Q5, Disp1.pin_10
  N20: U2.Q6, Disp1.pin_11
  N21: U2.Q7, Disp1.pin_12
  N22: U2.Q0, Disp1.pin_8

notes:
  Luckylight LED Matrix text on this side
  LED Matrix
  Microcontroller
  Shift Registers
  Button with       pulldown resistor
